# Fritzing sketch brewis (saved by Fritzing 0.9.0b)
breadboards: 1

parts:
  Arduino_UNO = Arduino Uno (Rev3)
  Relay = RELAY-SOLIDSTATE [package=relay-s108t02]
  DS1 = DS18B20 1-Wire Temperature Sensor [part_number=DS18B20]
  RN-41_Bluetooth = Bluetooth Module Breakout - Roving Networks (RN-41)
  LCD1 = LCD screen
  R1 = Resistor [tolerance=±5% resistance=1k package=THT]
  R2 = Resistor [tolerance=±5% resistance=220 package=THT]
  S1 = Pushbutton [package="[THT]"]
  S2 = Pushbutton [package="[THT]"]
  S3 = Pushbutton [package="[THT]"]
  R3 = Resistor [tolerance=±5% resistance=1k package=THT]
  R4 = Resistor [tolerance=±5% resistance=4.7k package=THT]
  R5 = Resistor [tolerance=±5% resistance=10k package=THT]
  R6 = Resistor [tolerance=±5% resistance=4.7k package=THT]
  R7 = Resistor [tolerance=±5% resistance=560 package=THT]
  R8 = Resistor [tolerance=±5% resistance=1k package=THT]
  HX711 = HX711 [package=THT]

nets:
  N1: Arduino_UNO.A0, S1.Pin_3, S1.Pin_4, S2.Pin_3, S2.Pin_4, S3.Pin_3, S3.Pin_4, R5.Pin_1
  N2: Arduino_UNO.A1, R2.Pin_0
  N3: Arduino_UNO.A2, HX711.DT
  N4: Arduino_UNO.A3, HX711.SCK
  N5: Arduino_UNO.D8, RN-41_Bluetooth.UARTTX
  N6: Arduino_UNO.D9_PWM, R8.Pin_0
  N7: Arduino_UNO.D11_PWM/MOSI, LCD1.E
  N8: Arduino_UNO.D12/MISO, LCD1.RS
  N9: Arduino_UNO.D2, LCD1.DB7
  N10: Arduino_UNO.D3_PWM, LCD1.DB6
  N11: Arduino_UNO.D4, LCD1.DB5
  N12: Arduino_UNO.D5_PWM, LCD1.DB4
  N13: Arduino_UNO.D6_PWM, DS1.DQ, R6.Pin_0
  N14: Arduino_UNO.D7, Relay.+
  3V3: Arduino_UNO.3V3, DS1.VDD, RN-41_Bluetooth.VCC, R6.Pin_1
  5V: Arduino_UNO.5V, LCD1.VDD, S3.Pin_1, S3.Pin_2, R3.Pin_0, R4.Pin_0, HX711.VCC
  GND: Arduino_UNO.GND, Relay.-, DS1.GND, RN-41_Bluetooth.GND, LCD1.VSS, LCD1.R/W, LCD1.LED-, R1.Pin_0, R5.Pin_0, R8.Pin_1, HX711.GND
  N15: RN-41_Bluetooth.UARTRX, R7.Pin_1
  N16: LCD1.V0, R1.Pin_1
  N17: LCD1.LED+, R2.Pin_1
  N18: S1.Pin_1, S1.Pin_2, R4.Pin_1
  N19: S2.Pin_1, S2.Pin_2, R3.Pin_1

notes:
  Bluetooth
  DS18B20
  Heating system relays
  HX711
  Button 1: LCD ON/OFF
  Button 2: heating enable/disable
  Button 3: data sender ON/OFF

custom parts:
  HX711: Scale amplifier/ADC
